# Fritzing sketch Fritzing (saved by Fritzing 0.9.3b)
breadboards: 1

parts:
  LED1 = Super Flux LED blue [color=Blue]  # not connected
  Netduino1 = Netduino Plus2

nets:
  N1: Netduino1.GND, Netduino1.D8_CTS1
